# Fritzing sketch Brazo robot 3D (saved by Fritzing 0.9.3b)
breadboards: 1

parts:
  S1 = H-Bridge with L298N
  Componente1 = Arduino Uno (Rev3)
  J1 = Basic Servo
  J2 = Basic Servo
  M1 = DC Motor
  Componente2 = Bluetooth HC-06 Macho

nets:
  GND: S1.GND, Componente1.GND, J1.gnd, J2.gnd, Componente2.GND
  VCC: S1.5V, Componente1.VIN, J1.vcc, J2.vcc, Componente2.VCC
  N1: S1.IN1, Componente1.D13/SCK
  N2: S1.OUT1-Motor1, M1.pin_1
  N3: S1.OUT2-Motor1, M1.pin_2
  N4: Componente1.D9_PWM, J1.pulse
  N5: Componente1.D2, Componente2.TXD
  N6: Componente1.D3_PWM, Componente2.RXD
  N7: Componente1.D6_PWM, J2.pulse

notes:
  Llevar alimentación +5 V y GND

custom parts:
  H-Bridge with L298N: h-bridge
